// Logisim project LOGICISM RAFAEL MELO.2.0.circ as structural Verilog: 5 circuits, main circuit main
module main (
  input  [3:0] in_1,
  input  [3:0] in_2,
  input  in_3,
  input  in_4,
  input  in_5,
  input  in_6,
  input  in_7,
  input  in_8,
  input  [3:0] in_9,
  input  [3:0] in_10,
  input  in_11,
  input  in_12,
  output out_13,
  output out_14,
  output out_15,
  output [3:0] out_16,
  output out_17,
  output out_18,
  output out_19,
  output [3:0] out_20
);

  SUB_1 sub_1_1 (.A(in_7), .B(in_8), .VEM_1(in_11), .S(out_18), .VAI_1(out_17));
  ADD add_1 (.A(in_3), .B(in_4), .VEM_1(in_5), .S(out_15), .VAI_1(out_13));
  sub_4 sub_4_1 (.in_1(in_9), .out_4(out_19), .in_2(in_10), .in_3(in_12), .out_5(out_20));
  ADD_4 add_4_1 (.B(in_2), .A(in_1), .VAI_1(out_14), .VEM_1(in_6), .S(out_16));
endmodule

// add_1
module ADD (
  input  A,
  input  B,
  input  VEM_1,
  output S,
  output VAI_1
);

  wire and_1_out, and_2_out, or_1_out, xor_1_out;

  xor xor_1 (xor_1_out, A, B);
  or or_1 (or_1_out, VEM_1, B);
  xor xor_2 (S, xor_1_out, VEM_1);
  and and_1 (and_1_out, A, or_1_out);
  and and_2 (and_2_out, B, VEM_1);
  or or_2 (VAI_1, and_1_out, and_2_out);
endmodule

// add_4
module ADD_4 (
  input  [3:0] B,
  input  [3:0] A,
  input  VEM_1,
  output VAI_1,
  output [3:0] S
);

  wire add_2_vai_1, add_3_vai_1, add_4_vai_1;

  ADD add_1 (.A(A[3]), .B(B[3]), .VEM_1(add_2_vai_1), .S(S[3]), .VAI_1(VAI_1));
  ADD add_2 (.A(A[2]), .B(B[2]), .VEM_1(add_3_vai_1), .S(S[2]), .VAI_1(add_2_vai_1));
  ADD add_3 (.A(A[1]), .B(B[1]), .VEM_1(add_4_vai_1), .S(S[1]), .VAI_1(add_3_vai_1));
  ADD add_4 (.A(A[0]), .B(B[0]), .VEM_1(VEM_1), .S(S[0]), .VAI_1(add_4_vai_1));
endmodule

module SUB_1 (
  input  A,
  input  B,
  input  VEM_1,
  output S,
  output VAI_1
);

  wire and_1_out, and_2_out, not_1_out, or_1_out, xor_1_out;

  and and_1 (and_1_out, B, VEM_1);
  xor xor_1 (xor_1_out, A, B);
  or or_1 (or_1_out, B, VEM_1);
  not not_1 (not_1_out, A);
  xor xor_2 (S, xor_1_out, VEM_1);
  and and_2 (and_2_out, or_1_out, not_1_out);
  or or_2 (VAI_1, and_1_out, and_2_out);
endmodule

module sub_4 (
  input  [3:0] in_1,
  input  [3:0] in_2,
  input  in_3,
  output out_4,
  output [3:0] out_5
);

  wire sub_1_2_vai_1, sub_1_3_vai_1, sub_1_4_vai_1;

  SUB_1 sub_1_1 (.A(in_1[3]), .B(in_2[3]), .VEM_1(sub_1_2_vai_1), .S(out_5[3]), .VAI_1(out_4));
  SUB_1 sub_1_2 (.A(in_1[2]), .B(in_2[2]), .VEM_1(sub_1_3_vai_1), .S(out_5[2]), .VAI_1(sub_1_2_vai_1));
  SUB_1 sub_1_3 (.A(in_1[1]), .B(in_2[1]), .VEM_1(sub_1_4_vai_1), .S(out_5[1]), .VAI_1(sub_1_3_vai_1));
  SUB_1 sub_1_4 (.A(in_1[0]), .B(in_2[0]), .VEM_1(in_3), .S(out_5[0]), .VAI_1(sub_1_4_vai_1));
endmodule
